# Fritzing sketch Gripper_MHC2-25D_Wiring_Diagram (saved by Fritzing 0.9.5d)

parts:
  U2 = 5-2 Solenoid Valve 24VDC 4V210-08
  MHC2-25D1 = MHC2-25D Pneumatic Gripper

nets:
  N1: U2.-, U2.Air_OUT_Open, MHC2-25D1.Air_IN_Open
  N2: U2.Air_OUT_Close, MHC2-25D1.Air_IN_Close
